# Fritzing sketch Untitled Sketch (saved by Fritzing 0.9.4)
breadboards: 1

parts:
  U1 = ESP8266 ESP-01 Upgraded WiFi Module [part_number=ESP8266]
  Part1 = Arduino Uno (Rev3)
  LED1 = smd LED [color="Red (633nm)" package="1206 [SMD]"]
  LED2 = smd LED [color="Blue (470nm)" package="1206 [SMD]"]
  LED3 = smd LED [color="Yellow (585nm)" package="1206 [SMD]"]
  R1 = Resistor [tolerance=±5% resistance=220 package="0603 [SMD]"]
  R2 = Resistor [tolerance=±5% resistance=220 package="0603 [SMD]"]
  R3 = Resistor [tolerance=±5% resistance=220 package="0603 [SMD]"]

nets:
  N1: U1.RXD, Part1.D3_PWM
  VCC: U1.VCC, U1.CH_PD, Part1.3V3
  GND: U1.GND, Part1.GND, LED1.cathode, LED2.cathode, LED3.cathode
  N2: U1.TXD, Part1.D2
  N3: Part1.D9_PWM, R3.Pin_0
  N4: Part1.D11_PWM/MOSI, R2.Pin_0
  N5: Part1.D13/SCK, R1.Pin_0
  N6: LED1.anode, R1.Pin_1
  N7: LED2.anode, R2.Pin_1
  N8: LED3.anode, R3.Pin_1

custom parts:
  ESP8266 ESP-01 Upgraded WiFi Module: Upgraded Version ESP-01,all Flash are upgraded to 1M byte.Also support Cloud service remote transmission.
